# Fritzing sketch DigitalLed-ESP32 (saved by Fritzing 0.9.4)
breadboards: 1

parts:
  U1 = Wemos Lolin D32
  R1 = Resistor [tolerance=±1% resistance=220 package=THT]
  LED1 = LED - 5mm [color="Red (633nm)" package="5 mm [THT]"]

nets:
  N1: U1.pin_16, U1.pin_17
  N2: U1.pin_18, U1.pin_33, R1.Pin_1
  N3: U1.pin_26, LED1.cathode
  N4: R1.Pin_0, LED1.anode

custom parts:
  Wemos Lolin D32: Wemos Lolin D32 wifi and blue tooth board based on the ESP-32 cpu, digital I/Os 22, analog inputs 6, analog outputs 2 clock 240mhz, Flash 4Mbytes, lipo battery charger (500ma connection broken out on breadboard but not pcb), usb. The mounting holes are only set on the silkscreen, if you want actual holes in the pcb copy the hole from the pcb menu in parts over the top of the hole in the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
