# Fritzing sketch Ldr-ESP32 (saved by Fritzing 0.9.3b)
breadboards: 1

parts:
  U1 = Wemos Lolin D32
  R1 = Resistor [tolerance=±1% resistance=10k package=THT]
  R2 = Photocell (LDR) [package=THT]

nets:
  N1: U1.pin_1, R1.Pin_1
  N2: U1.pin_8, R1.Pin_0, R2.pin_1
  N3: U1.pin_16, U1.pin_17
  N4: U1.pin_18, U1.pin_33
  N5: U1.pin_32, R2.pin_0

custom parts:
  Wemos Lolin D32: Wemos Lolin D32 wifi and blue tooth board based on the ESP-32 cpu, digital I/Os 22, analog inputs 6, analog outputs 2 clock 240mhz, Flash 4Mbytes, lipo battery charger (500ma connection broken out on breadboard but not pcb), usb. The mounting holes are only set on the silkscreen, if you want actual holes in the pcb copy the hole from the pcb menu in parts over the top of the hole in the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
