# Fritzing sketch Max30102-ESP32 (saved by Fritzing 0.9.4)
breadboards: 1

parts:
  U1 = Wemos Lolin D32
  M1 = MakerFocus MAX30102

nets:
  N1: U1.pin_0, M1.INT
  N2: U1.pin_16, U1.pin_17
  N3: U1.pin_18, U1.pin_33, M1.GND
  N4: U1.pin_28, M1.IRQ
  N5: U1.pin_31, M1.RD

custom parts:
  Wemos Lolin D32: Wemos Lolin D32 wifi and blue tooth board based on the ESP-32 cpu, digital I/Os 22, analog inputs 6, analog outputs 2 clock 240mhz, Flash 4Mbytes, lipo battery charger (500ma connection broken out on breadboard but not pcb), usb. The mounting holes are only set on the silkscreen, if you want actual holes in the pcb copy the hole from the pcb menu in parts over the top of the hole in the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
  MakerFocus MAX30102: Oximeter module using the MAX30102 chip. As usual, if you want the mounting holes in pcb, you need to drag a hole over the pad in silkscreen to actually drill the hole (by default they are not drilled)
